# Fritzing sketch VCO_Sawtooth (saved by Fritzing 0.9.3b)
breadboards: 2

parts:
  IC1 = Dual Op-Amp [package=dip08]
  Q1 = NPN-Transistor [package="TO92 [THT]"]
  R1 = Resistor [tolerance=±5% resistance=22k package=THT]
  D1 = Rectifier Diode [part_number=1N4001 package="300 mil [THT]"]
  R3 = Resistor [tolerance=±5% resistance=100k package=THT]
  Q2 = Basic FET N-Channel [package="TO220 [THT]"]
  IC2 = Dual Op-Amp [package=dip08]
  C1 = Ceramic Capacitor [capacitance=100nF package="100 mil [THT, multilayer]"]
  R4 = Resistor [tolerance=±5% resistance=10k package=THT]
  R5 = Resistor [tolerance=±5% resistance=10k package=THT]
  C2 = Ceramic Capacitor [capacitance=100nF package="100 mil [THT, multilayer]"]
  C3 = Ceramic Capacitor [capacitance=100nF package="100 mil [THT, multilayer]"]
  C4 = Ceramic Capacitor [capacitance=100nF package="100 mil [THT, multilayer]"]
  C5 = Ceramic Capacitor [capacitance=100nF package="100 mil [THT, multilayer]"]
  C6 = Ceramic Capacitor [capacitance=100nF package="100 mil [THT, multilayer]"]
  C7 = Electrolytic Capacitor [capacitance=1µF package="100 mil [THT, electrolytic]"]
  C8 = Electrolytic Capacitor [capacitance=1µF package="100 mil [THT, electrolytic]"]
  Q3 = Basic FET P-Channel [package="TO220 [THT]"]
  R6 = Rotary Potentiometer (Small) [maximum_resistance=100kΩ package=THT]
  IC3 = Dual Op-Amp [package=dip08]
  R7 = TRIMPOT [package=trimpot_pth_s3_lock]
  C9 = Ceramic Capacitor [capacitance=100nF package="100 mil [THT, multilayer]"]
  C10 = Ceramic Capacitor [capacitance=100nF package="100 mil [THT, multilayer]"]

nets:
  N1: IC1.A_OUT, Q1.C
  N2: IC1.A_-IN, R5.Pin_0, C2.1
  N3: IC1.A_+IN, R4.Pin_0
  N4: IC1.A_V-, Q1.E, IC2.A_V-, C3.0, C6.0, C8.-, Q3.drain, Q3.source, R6.leg1, R6.wiper, R6.leg2, IC3.A_V-, C10.0
  N5: IC1.B_+IN, IC2.B_+IN, R5.Pin_1, C3.1, C4.0, C5.0, C6.1, C7.-, C8.+, IC3.B_+IN, R7.CW, C9.0, C10.1
  N6: IC1.B_-IN, IC1.B_OUT
  N7: IC1.A_V+, R1.Pin_0, IC2.A_V+, C4.1, C5.1, C7.+, IC3.A_V+, R7.CCW, C9.1
  N8: Q1.B, R1.Pin_1, D1.cathode, C2.0
  N9: D1.anode, R3.Pin_1, Q2.drain
  N10: R3.Pin_0, Q2.gate, C1.1, IC3.A_OUT, IC3.A_-IN
  N11: Q2.source, IC2.A_+IN, C1.0, Q3.gate
  N12: IC2.A_OUT, IC2.A_-IN, R4.Pin_1
  N13: IC2.B_-IN, IC2.B_OUT
  N14: IC3.A_+IN, R7.WIPER
  N15: IC3.B_-IN, IC3.B_OUT

notes:
  2SK170
  D / G / S
  VREF
  Adj. 5V
  SAW_OUT
  VEE
  GND
  GND
  VCC
  JFET
  吸い込み型電流源
  ※いつも間違えますが、GATEをGND(VEE)。
  GATE-SOURCE間にR
  VEE
  NC
