# Fritzing sketch VCO_Sawtooth_2 (saved by Fritzing 0.9.3b)
breadboards: 2

parts:
  IC1 = Dual Op-Amp [package=dip08]
  Q1 = Basic FET P-Channel [package="TO220 [THT]"]
  R1 = Rotary Potentiometer (Small) [maximum_resistance=100kΩ package=THT]
  Q2 = PNP-Transistor [package="TO92 [THT]"]
  C1 = Ceramic Capacitor [capacitance=100nF package="100 mil [THT, multilayer]"]
  IC2 = Dual Op-Amp [package=dip08]
  R2 = Resistor [tolerance=±5% resistance=120k package=THT]
  C2 = Ceramic Capacitor [capacitance=100nF package="100 mil [THT, multilayer]"]
  C3 = Ceramic Capacitor [capacitance=100nF package="100 mil [THT, multilayer]"]
  R3 = Resistor [tolerance=±5% resistance=100k package=THT]
  R4 = Resistor [tolerance=±5% resistance=150 package=THT]
  C4 = Ceramic Capacitor [capacitance=100nF package="100 mil [THT, multilayer]"]
  C5 = Ceramic Capacitor [capacitance=100nF package="100 mil [THT, multilayer]"]
  C6 = Ceramic Capacitor [capacitance=100nF package="100 mil [THT, multilayer]"]
  R5 = Resistor [tolerance=±5% resistance=10k package=THT]
  R6 = Resistor [tolerance=±5% resistance=680 package=THT]
  R7 = Resistor [tolerance=±5% resistance=100k package=THT]
  R8 = Resistor [tolerance=±5% resistance=100k package=THT]
  IC3 = Dual Op-Amp [package=dip08]
  R9 = TRIMPOT [package=trimpot_pth_s3_lock]
  C7 = Ceramic Capacitor [capacitance=100nF package="100 mil [THT, multilayer]"]
  C8 = Ceramic Capacitor [capacitance=100nF package="100 mil [THT, multilayer]"]
  C9 = Electrolytic Capacitor [capacitance=1µF package="100 mil [THT, electrolytic]"]
  C10 = Electrolytic Capacitor [capacitance=1µF package="100 mil [THT, electrolytic]"]

nets:
  N1: IC1.A_OUT, R2.Pin_0, R8.Pin_1
  N2: IC1.A_-IN, R2.Pin_1, R3.Pin_0
  N3: IC1.A_+IN, Q1.gate, Q2.B, C1.0
  N4: IC1.A_V-, Q1.drain, Q1.source, R1.leg1, R1.wiper, R1.leg2, IC2.A_V-, C3.0, C5.0, IC3.A_V-, C8.0, C10.-
  N5: IC1.B_+IN, IC2.B_+IN, C2.0, C3.1, C4.0, C5.1, R5.Pin_1, IC3.B_+IN, R9.CW, C7.0, C8.1, C9.-, C10.+
  N6: IC1.B_-IN, IC1.B_OUT
  N7: IC1.A_V+, IC2.A_V+, C2.1, C4.1, IC3.A_V+, R9.CCW, C7.1, C9.+
  N8: Q2.E, C1.1, R3.Pin_1, R4.Pin_0, R7.Pin_0, IC3.A_OUT, IC3.A_-IN
  N9: Q2.C, R4.Pin_1, R6.Pin_0
  N10: IC2.A_OUT, C6.0, R6.Pin_1
  N11: IC2.A_-IN, R5.Pin_0
  N12: IC2.A_+IN, C6.1, R7.Pin_1, R8.Pin_0
  N13: IC2.B_-IN, IC2.B_OUT
  N14: IC3.A_+IN, R9.WIPER
  N15: IC3.B_-IN, IC3.B_OUT

notes:
  2SK170
  D / G / S
  VEE
  NC
  JFET
  吸い込み型電流源
  VREF
  Adj. 5V
  SAW_OUT
  2SA1015
  E / C / B
  ※いつも間違えますが、GATEをGND(VEE)。
  GATE-SOURCE間にR
