# Fritzing sketch SAW_TRI_RayWilson_01 (saved by Fritzing 0.9.3b)
breadboards: 1

parts:
  IC1 = Dual Op-Amp [package=dip08]
  D1 = Rectifier Diode [part_number=1N4001 package="300 mil [THT]"]
  R1 = Resistor [tolerance=±5% resistance=10k package=THT]
  R2 = Resistor [tolerance=±5% resistance=20k package=THT]
  IC2 = Dual Op-Amp [package=dip08]
  R3 = Resistor [tolerance=±5% resistance=10k package=THT]
  D2 = Rectifier Diode [part_number=1N4001 package="300 mil [THT]"]
  C1 = Ceramic Capacitor [capacitance=100nF package="100 mil [THT, multilayer]"]
  C2 = Ceramic Capacitor [capacitance=100nF package="100 mil [THT, multilayer]"]
  C3 = Ceramic Capacitor [capacitance=100nF package="100 mil [THT, multilayer]"]
  C4 = Ceramic Capacitor [capacitance=100nF package="100 mil [THT, multilayer]"]
  C5 = Electrolytic Capacitor [capacitance=1µF package="100 mil [THT, electrolytic]"]
  C6 = Electrolytic Capacitor [capacitance=1µF package="100 mil [THT, electrolytic]"]

nets:
  N1: IC1.A_OUT, D1.anode, R1.Pin_0
  N2: IC1.A_-IN, R1.Pin_1, R3.Pin_0
  N3: IC1.A_+IN, IC1.B_+IN, IC2.B_+IN, C1.0, C2.0, C3.1, C4.1, C5.-, C6.-
  N4: IC1.A_V-, R2.Pin_1, IC2.A_V-, C3.0, C4.0, C6.+
  N5: IC1.B_-IN, IC1.B_OUT
  N6: IC1.A_V+, IC2.A_V+, C1.1, C2.1, C5.+
  N7: D1.cathode, R2.Pin_0, D2.cathode
  N8: IC2.A_OUT, IC2.A_-IN, R3.Pin_1, D2.anode
  N9: IC2.B_-IN, IC2.B_OUT

notes:
  SAW IN
  TRI OUT
  GND
  VCC
  VEE
  GND
