# Fritzing sketch Hysteresis_Comparator (saved by Fritzing 0.9.3b)
breadboards: 1

parts:
  IC1 = Dual Op-Amp [package=dip08]
  R1 = Resistor [tolerance=±5% resistance=10k package=THT]
  R2 = Resistor [tolerance=±5% resistance=10k package=THT]
  R3 = Resistor [tolerance=±5% resistance=100k package=THT]
  C1 = Ceramic Capacitor [capacitance=100nF package="100 mil [THT, multilayer]"]
  C2 = Ceramic Capacitor [capacitance=100nF package="100 mil [THT, multilayer]"]
  C3 = Electrolytic Capacitor [capacitance=1µF package="100 mil [THT, electrolytic]"]
  C4 = Electrolytic Capacitor [capacitance=1µF package="100 mil [THT, electrolytic]"]
  IC2 = Dual Op-Amp [package=dip08]
  R4 = TRIMPOT [package=trimpot_pth_s3_lock]
  C5 = Ceramic Capacitor [capacitance=100nF package="100 mil [THT, multilayer]"]
  C6 = Ceramic Capacitor [capacitance=100nF package="100 mil [THT, multilayer]"]
  C7 = Electrolytic Capacitor [capacitance=1µF package="100 mil [THT, electrolytic]"]
  R5 = Resistor [tolerance=±5% resistance=10k package=THT]

nets:
  N1: IC1.A_OUT, R3.Pin_1
  N2: IC1.A_-IN, IC2.A_OUT, IC2.A_-IN
  N3: IC1.A_+IN, R1.Pin_0, R2.Pin_1, R3.Pin_0
  N4: IC1.A_V-, C1.0, C4.-, IC2.A_V-, C5.0
  N5: IC1.B_+IN, R1.Pin_1, C1.1, C2.0, C3.-, C4.+, IC2.B_+IN, R4.CW, C5.1, C6.0, R5.Pin_1
  N6: IC1.B_-IN, IC1.B_OUT
  N7: IC1.A_V+, R2.Pin_0, C2.1, C3.+, IC2.A_V+, R4.CCW, C6.1
  N8: IC2.A_+IN, R4.WIPER, C7.+, R5.Pin_0
  N9: IC2.B_-IN, IC2.B_OUT

notes:
  Tri In
  1k Ohm
  Adj. +5V
  OUT
  GND
  +12V
  -12V
  GND
