# Fritzing sketch VCO_VCO_NoLimit (saved by Fritzing 0.9.3b)
breadboards: 1

parts:
  IC1 = Dual Op-Amp [package=dip08]
  R1 = Resistor [tolerance=±5% resistance=10k package=THT]
  R2 = Resistor [tolerance=±5% resistance=10k package=THT]
  R3 = Resistor [tolerance=±5% resistance=100k package=THT]
  C1 = Ceramic Capacitor [capacitance=100nF package="100 mil [THT, multilayer]"]
  C2 = Ceramic Capacitor [capacitance=100nF package="100 mil [THT, multilayer]"]
  C3 = Electrolytic Capacitor [capacitance=1µF package="100 mil [THT, electrolytic]"]
  C4 = Electrolytic Capacitor [capacitance=1µF package="100 mil [THT, electrolytic]"]
  IC2 = Dual Op-Amp [package=dip08]
  C5 = Ceramic Capacitor [capacitance=100nF package="100 mil [THT, multilayer]"]
  C6 = Ceramic Capacitor [capacitance=100nF package="100 mil [THT, multilayer]"]
  R4 = Resistor [tolerance=±5% resistance=47k package=THT]
  R5 = Resistor [tolerance=±5% resistance=47k package=THT]
  R6 = Resistor [tolerance=±5% resistance=100k package=THT]
  R7 = Resistor [tolerance=±5% resistance=47k package=THT]
  Q1 = NPN-Transistor [package="TO92 [THT]"]
  R8 = Resistor [tolerance=±5% resistance=10k package=THT]
  R9 = Rotary Potentiometer (Small) [maximum_resistance=100kΩ package=THT]
  R10 = Resistor [tolerance=±5% resistance=10k package=THT]
  C7 = Ceramic Capacitor [capacitance=100nF package="100 mil [THT, multilayer]"]

nets:
  N1: IC1.A_OUT, R3.Pin_0, R8.Pin_1
  N2: IC1.A_+IN, R1.Pin_0, R2.Pin_1, R3.Pin_1, IC2.A_OUT, C7.0
  N3: IC1.A_V-, C1.0, C4.-, IC2.A_V-, C5.0
  N4: IC1.B_+IN, C2.0, C3.-, IC2.B_+IN, C6.0
  N5: IC1.B_-IN, IC1.B_OUT
  N6: IC1.A_V+, R2.Pin_0, C2.1, C3.+, IC2.A_V+, C6.1, R10.Pin_0
  N7: R1.Pin_1, C1.1, C4.+, C5.1, R4.Pin_1, Q1.E, R9.leg1
  N8: IC2.A_-IN, R6.Pin_0, R7.Pin_1, C7.1
  N9: IC2.A_+IN, R4.Pin_0, R5.Pin_0
  N10: IC2.B_-IN, IC2.B_OUT
  N11: R5.Pin_1, R6.Pin_1, R9.wiper
  N12: R7.Pin_0, Q1.B
  N13: Q1.C, R8.Pin_0
  N14: R9.leg2, R10.Pin_1

notes:
  SQROUT
  GND
  +12V
  -12V
  GND
  CV
  10k/B
  TRIOUT
